# Fritzing sketch totem_panic (saved by Fritzing 0.9.2b)
breadboards: 1

parts:
  Composant1 = Arduino Uno (Rev3) - ICSP
  J1 = Basic Servo
  J2 = Basic Servo
  J3 = Basic Servo
  J4 = Basic Servo

nets:
  GND: Composant1.GND, J1.gnd, J2.gnd, J3.gnd, J4.gnd
  N1: Composant1.D9_PWM, J4.pulse
  N2: Composant1.D3_PWM, J3.pulse
  N3: Composant1.D5_PWM, J1.pulse
  N4: Composant1.D6_PWM, J2.pulse
  VCC: J1.vcc, J2.vcc, J3.vcc, J4.vcc
